// Logisim project PROJ1-NAND.circ as structural Verilog: 1 circuit, main circuit main
module main (
  input  A,
  input  B,
  input  C,
  output out_4
);

  wire A_prime_B_prime_C_out, A_prime_BC_out, AA_prime_out, AB_prime_C_out, AB_prime_C_prime_out, ABC_out,
       BB_prime_out, CC_prime_out;

  nand AA_prime (AA_prime_out, A, A);
  nand BB_prime (BB_prime_out, B, B);
  nand CC_prime (CC_prime_out, C, C);
  nand A_prime_BC (A_prime_BC_out, C, AA_prime_out, B);
  nand ABC (ABC_out, A, B, C);
  nand AB_prime_C_prime (AB_prime_C_prime_out, A, BB_prime_out, CC_prime_out);
  nand AB_prime_C (AB_prime_C_out, BB_prime_out, A, C);
  nand A_prime_B_prime_C (A_prime_B_prime_C_out, AA_prime_out, BB_prime_out, C);
  nand F (out_4, A_prime_BC_out, AB_prime_C_out, ABC_out, AB_prime_C_prime_out, A_prime_B_prime_C_out);

  // Notes on the sheet:
  //   '
endmodule
