// Logisim project OR.circ as structural Verilog: 1 circuit, main circuit proj1
module proj1 (
  input  A,
  input  B,
  input  C
);

  wire A_prime_B_prime_C_prime_out, A_prime_BC_out, AB_prime_C_out, AB_prime_C_prime_out, ABC_out, F_out,
       not_1_out, not_2_out, not_3_out;

  not not_1 (not_1_out, A);
  not not_2 (not_2_out, B);
  not not_3 (not_3_out, C);
  and A_prime_BC (A_prime_BC_out, C, not_1_out, B);
  and ABC (ABC_out, A, B, C);
  and AB_prime_C_prime (AB_prime_C_prime_out, A, not_2_out, not_3_out);
  and AB_prime_C (AB_prime_C_out, not_2_out, A, C);
  and A_prime_B_prime_C_prime (A_prime_B_prime_C_prime_out, not_1_out, not_2_out, C);
  or F (F_out, A_prime_BC_out, AB_prime_C_out, ABC_out, AB_prime_C_prime_out, A_prime_B_prime_C_prime_out);

  // Notes on the sheet:
  //   A'
  //   B'
  //   C'
endmodule
